// Logisim project alu.circ as structural Verilog: 1 circuit, main circuit alu
module alu (
  input  [31:0] A,
  input  [31:0] B,
  input  [3:0] ALUSel,
  output [31:0] Result
);

  wire adder_2_cout, comparator_1_lt;
  wire [31:0] adder_1_out, adder_2_out, adder_3_out, and_1_out, bit_extender_1_out, divider_1_out,
       divider_1_rem, multiplier_1_cout, multiplier_1_out, multiplier_2_out, multiplier_3_out, or_1_out,
       shifter_1_out, shifter_2_out, shifter_3_out, shifter_4_out, shifter_5_out, subtractor_2_out, xor_1_out;

  Adder #(.width(32)) adder_1 (.a(A), .b(B), .out(adder_1_out));  // open: cin, cout
  Subtractor #(.width(32)) subtractor_1 (.a(A), .b(B));  // open: out, bin, bout
  assign and_1_out = A & B;  // AND_Gate and_1, 32 bits wide
  assign or_1_out = A | B;  // OR_Gate or_1, 32 bits wide
  assign xor_1_out = A ^ B;  // XOR_Gate xor_1, 32 bits wide
  Comparator #(.width(32)) comparator_1 (.a(A), .b(B), .lt(comparator_1_lt));  // open: gt, eq
  assign bit_extender_1_out = {{31{1'b0}}, comparator_1_lt};  // Bit_Extender bit_extender_1
  Divider #(.width(32)) divider_1 (.a(A), .b(B), .out(divider_1_out), .rem(divider_1_rem));  // open: upper
  Multiplier #(.width(32)) multiplier_1 (.a(A), .b(B), .out(multiplier_1_out), .cout(multiplier_1_cout));  // open: cin
  Subtractor #(.width(32)) subtractor_2 (.a(A), .b(B), .out(subtractor_2_out));  // open: bin, bout
  Shifter #(.width(32), .shift("ar")) shifter_1 (.in(A), .\dist ({5{1'b1}}), .out(shifter_1_out));
  Shifter #(.width(32), .shift("ar")) shifter_2 (.in(B), .\dist ({5{1'b1}}), .out(shifter_2_out));
  Shifter #(.width(32), .shift("lr")) shifter_3 (.in(A), .\dist (B[4:0]), .out(shifter_3_out));
  Shifter #(.width(32), .shift("ar")) shifter_4 (.in(A), .\dist (B[4:0]), .out(shifter_4_out));
  Shifter #(.width(32)) shifter_5 (.in(A), .\dist (B[4:0]), .out(shifter_5_out));
  Multiplier #(.width(32)) multiplier_2 (.a(shifter_1_out), .b(B), .out(multiplier_2_out));  // open: cin, cout
  Multiplier #(.width(32)) multiplier_3 (.a(A), .b(shifter_2_out), .out(multiplier_3_out));  // open: cin, cout
  Adder #(.width(32)) adder_2 (
    .a(multiplier_2_out), .b(multiplier_3_out), .out(adder_2_out), .cout(adder_2_cout));  // open: cin
  Adder #(.width(32)) adder_3 (
    .a(adder_2_out), .b(multiplier_1_cout), .out(adder_3_out), .cin(adder_2_cout));  // open: cout
  Multiplexer #(.select(4), .width(32), .enable("false")) multiplexer_1 (
    .in0(adder_1_out), .in1(and_1_out), .in2(or_1_out), .in3(xor_1_out), .in4(shifter_3_out),
    .in5(shifter_4_out), .in6(shifter_5_out), .in7(bit_extender_1_out), .in8(divider_1_out),
    .in9(divider_1_rem), .in10(multiplier_1_out), .in11(multiplier_1_cout), .in12(subtractor_2_out),
    .in13(B), .in14(adder_3_out), .out(Result), .sel(ALUSel));  // open: in15

  // Notes on the sheet:
  //   INPUTS to your circuit
  //   DON'T CHANGE THE LOCATIONS OF THE INPUTS AND OUTPUTS!
  //   OUTPUT from your circuit
endmodule
