// Logisim project control_logic.circ as structural Verilog: 1 circuit, main circuit control_logic
module control_logic (
  input  [31:0] inst,
  input  BrEq,
  input  BrLt,
  output PCSel,
  output RegWEn,
  output [2:0] ImmSel,
  output BrUn,
  output ASel,
  output BSel,
  output [3:0] ALUSel,
  output MemRW,
  output [1:0] WBSel
);

  wire and_1_out, and_2_out, and_3_out, and_4_out, and_5_out, and_6_out, and_7_out, and_8_out, and_9_out,
       and_10_out, and_11_out, and_12_out, and_13_out, and_14_out, and_15_out, and_16_out, and_17_out,
       and_18_out, and_19_out, and_20_out, and_21_out, and_22_out, and_24_out, and_25_out, comparator_1_eq,
       comparator_2_eq, comparator_3_eq, decoder_1_out0, decoder_1_out1, decoder_1_out2, decoder_1_out3,
       decoder_1_out4, decoder_1_out5, decoder_1_out6, decoder_1_out7, decoder_2_out0, decoder_2_out1,
       decoder_2_out2, decoder_2_out4, decoder_2_out5, decoder_2_out6, decoder_2_out7, funct7_0, funct7_1,
       funct7_20, is_i, is_r, is_s, is_sb, is_u, is_uj, multiplexer_4_out, not_1_out, not_2_out, not_3_out,
       op03, op13, op17, op37, op67, or_1_out, or_2_out, or_3_out, or_4_out, or_9_out, or_10_out;
  wire [1:0] priority_encoder_1_out;
  wire [2:0] priority_encoder_5_out;
  wire [3:0] multiplexer_1_out, priority_encoder_2_out, priority_encoder_3_out, priority_encoder_4_out;

  Decoder #(.select(3)) decoder_1 (
    .out0(decoder_1_out0), .out1(decoder_1_out1), .out2(decoder_1_out2), .out3(decoder_1_out3),
    .out4(decoder_1_out4), .out5(decoder_1_out5), .out6(decoder_1_out6), .out7(decoder_1_out7),
    .sel(inst[14:12]));  // open: en
  Comparator #(.width(7), .mode("unsigned")) comparator_1 (
    .a(inst[31:25]), .b(7'b0100000), .eq(comparator_1_eq));  // open: gt, lt
  Comparator #(.width(7), .mode("unsigned")) comparator_2 (
    .a(inst[31:25]), .b(7'b0000001), .eq(comparator_2_eq));  // open: gt, lt
  Comparator #(.width(7), .mode("unsigned")) comparator_3 (
    .a(inst[31:25]), .b({7{1'b0}}), .eq(comparator_3_eq));  // open: gt, lt
  Decoder #(.select(3)) decoder_2 (
    .out0(decoder_2_out0), .out1(decoder_2_out1), .out2(decoder_2_out2), .out4(decoder_2_out4),
    .out5(decoder_2_out5), .out6(decoder_2_out6), .out7(decoder_2_out7), .sel(inst[14:12]));  // open: out3, en
  or or_1 (or_1_out, op67, op13);
  Multiplexer #(.select(2), .width(4), .enable("false")) multiplexer_1 (
    .in0(4'b0000), .in1(4'b1010), .in2(4'b1100), .out(multiplexer_1_out), .sel(priority_encoder_1_out));  // open: in3
  Priority_Encoder #(.select(2)) priority_encoder_1 (
    .in0(funct7_0), .in1(funct7_1), .in2(funct7_20), .out(priority_encoder_1_out));  // open: in3, gs, en_out, en_in
  and and_1 (and_1_out, or_1_out, decoder_2_out0);
  and and_2 (and_2_out, or_1_out, decoder_2_out7);
  and and_3 (and_3_out, or_1_out, decoder_2_out6);
  and and_4 (and_4_out, or_1_out, decoder_2_out4);
  and and_5 (and_5_out, or_1_out, comparator_3_eq, decoder_2_out5);
  and and_6 (and_6_out, decoder_2_out5, comparator_1_eq, or_1_out);
  and and_7 (and_7_out, decoder_2_out1, or_1_out, comparator_3_eq);
  and and_8 (and_8_out, decoder_2_out2, or_1_out);
  or or_2 (or_2_out, decoder_2_out6, decoder_2_out7);
  and and_9 (and_9_out, decoder_1_out0, comparator_3_eq);
  and and_10 (and_10_out, decoder_1_out7, comparator_3_eq);
  and and_11 (and_11_out, decoder_1_out6, comparator_3_eq);
  and and_12 (and_12_out, decoder_1_out4, comparator_3_eq);
  and and_13 (and_13_out, decoder_1_out5, comparator_3_eq);
  and and_14 (and_14_out, decoder_1_out5, comparator_1_eq);
  and and_15 (and_15_out, decoder_1_out1, comparator_3_eq);
  and and_16 (and_16_out, decoder_1_out2, comparator_3_eq);
  and and_17 (and_17_out, decoder_1_out5, comparator_2_eq);
  and and_18 (and_18_out, decoder_1_out7, comparator_2_eq);
  and and_19 (and_19_out, comparator_2_eq, decoder_1_out0);
  and and_20 (and_20_out, decoder_1_out3, comparator_2_eq);
  and and_21 (and_21_out, decoder_1_out0, comparator_1_eq);
  and and_22 (and_22_out, decoder_1_out1, comparator_2_eq);
  and and_23 (BrUn, or_2_out, is_sb);
  or or_3 (or_3_out, BrLt, not_1_out);
  not not_1 (not_1_out, decoder_1_out7);
  Comparator #(.width(7), .mode("unsigned")) comparator_4 (
    .a({7{1'b0}}), .b(inst[31:25]), .eq(funct7_0));  // open: gt, lt
  Comparator #(.width(7), .mode("unsigned")) comparator_5 (
    .a(7'b0000001), .b(inst[31:25]), .eq(funct7_1));  // open: gt, lt
  Comparator #(.width(7), .mode("unsigned")) comparator_6 (
    .a(7'b0100000), .b(inst[31:25]), .eq(funct7_20));  // open: gt, lt
  and and_24 (and_24_out, is_s, or_3_out);
  or or_4 (or_4_out, op03, and_1_out);
  Multiplexer #(.select(3), .width(4), .enable("false")) multiplexer_2 (
    .in0(multiplexer_1_out), .sel(inst[14:12]));  // open: in1, in2, in3, in4, in5, in6, in7, out
  or or_5 (MemRW, op03, and_24_out);
  Priority_Encoder #(.select(4)) priority_encoder_2 (
    .in0(and_9_out), .in1(and_10_out), .in2(and_11_out), .in3(and_12_out), .in4(and_13_out),
    .in5(and_14_out), .in6(and_15_out), .in7(and_16_out), .in8(and_17_out), .in9(and_18_out),
    .in10(and_19_out), .in11(and_20_out), .in12(and_21_out), .in14(and_22_out), .out(priority_encoder_2_out));  // open: in13, in15, gs, en_out, en_in
  Priority_Encoder #(.select(4)) priority_encoder_3 (
    .in0(or_4_out), .in1(and_2_out), .in2(and_3_out), .in3(and_4_out), .in4(and_5_out), .in5(and_6_out),
    .in6(and_7_out), .in7(and_8_out), .out(priority_encoder_3_out));  // open: in8, in9, in10, in11, in12, in13, in14, in15, gs, en_out, en_in
  Priority_Encoder #(.select(4)) priority_encoder_4 (
    .in0(decoder_2_out2), .in13(decoder_2_out7), .out(priority_encoder_4_out));  // open: in1, in2, in3, in4, in5, in6, in7, in8, in9, in10, in11, in12, in14, in15, gs, en_out, en_in
  Multiplexer #(.select(3), .width(4), .enable("false")) multiplexer_3 (
    .in0(priority_encoder_2_out), .in1(priority_encoder_3_out), .in2(priority_encoder_4_out), .in3(4'b0000),
    .in4(4'b0000), .in5(4'b1101), .in6(4'b0000), .out(ALUSel), .sel(priority_encoder_5_out));  // open: in7
  Priority_Encoder priority_encoder_5 (
    .in0(is_r), .in1(is_i), .in2(is_s), .in3(is_sb), .in4(op17), .in5(op37), .in6(is_uj),
    .out(priority_encoder_5_out));  // open: in7, en_in, gs, en_out
  Comparator #(.width(7), .mode("unsigned")) comparator_7 (.a(inst[6:0]), .b(7'b0110011), .eq(is_r));  // open: gt, lt
  Comparator #(.width(7), .mode("unsigned")) comparator_8 (.a(inst[6:0]), .b(7'b0000011), .eq(op03));  // open: gt, lt
  Comparator #(.width(7), .mode("unsigned")) comparator_9 (.a(inst[6:0]), .b(7'b0010011), .eq(op13));  // open: gt, lt
  Comparator #(.width(7), .mode("unsigned")) comparator_10 (.a(inst[6:0]), .b(7'b0100011), .eq(is_s));  // open: gt, lt
  Comparator #(.width(7), .mode("unsigned")) comparator_11 (.a(inst[6:0]), .b(7'b1100011), .eq(is_sb));  // open: gt, lt
  Comparator #(.width(7), .mode("unsigned")) comparator_12 (.a(inst[6:0]), .b(7'b0010111), .eq(op17));  // open: gt, lt
  Comparator #(.width(7), .mode("unsigned")) comparator_13 (.a(inst[6:0]), .b(7'b0110111), .eq(op37));  // open: gt, lt
  Comparator #(.width(7), .mode("unsigned")) comparator_14 (.a(inst[6:0]), .b(7'b1101111), .eq(is_uj));  // open: gt, lt
  not not_2 (not_2_out, BrEq);
  not not_3 (not_3_out, BrLt);
  or or_6 (is_i, op03, op67, op13);
  Comparator #(.width(7), .mode("unsigned")) comparator_15 (.a(inst[6:0]), .b(7'b1100111), .eq(op67));  // open: gt, lt
  or or_7 (is_u, op17, op37);
  Multiplexer #(.select(3), .enable("false")) multiplexer_4 (
    .in0(BrEq), .in1(not_2_out), .in4(BrLt), .in5(not_3_out), .in6(BrLt), .in7(not_3_out),
    .out(multiplexer_4_out), .sel(inst[14:12]));  // open: in2, in3
  Priority_Encoder priority_encoder_6 (
    .in0(is_i), .in1(is_s), .in2(is_sb), .in3(is_u), .in4(is_uj), .out(ImmSel));  // open: in5, in6, in7, en_in, gs, en_out
  or or_8 (RegWEn, is_i, is_r, is_u, is_uj);
  or or_9 (or_9_out, is_uj, op67);
  and and_25 (and_25_out, is_sb, multiplexer_4_out);
  or or_10 (or_10_out, is_r, is_u, op13);
  or or_11 (ASel, is_u, is_sb, is_uj);
  not not_4 (BSel, is_r);
  or or_12 (PCSel, is_uj, and_25_out, op67);
  Priority_Encoder #(.select(2)) priority_encoder_7 (
    .in0(or_10_out), .in1(op03), .in2(or_9_out), .out(WBSel));  // open: in3, gs, en_out, en_in

  // Other names for the same wires on the sheet: opcode[6:0] = inst[6:0]; funct3[2:0] = inst[14:12];
  //   funct7[6:0] = inst[31:25]

  // Notes on the sheet:
  //   INPUTS to your circuit
  //   DON'T CHANGE THE LOCATIONS OF THE INPUTS AND OUTPUTS!
  //   OUTPUT from your circuit
endmodule
