// Logisim project cpu.circ as structural Verilog: 1 circuit, main circuit main
module main (
  input  [31:0] INSTRUCTION,
  input  in_2,
  output [31:0] PROGRAM_COUNTER,
  output [31:0] ra,
  output [31:0] sp,
  output [31:0] t0,
  output [31:0] t1,
  output [31:0] t2,
  output [31:0] s0,
  output [31:0] s1,
  output [31:0] a0
);

  wire branch_comp_1_breq, branch_comp_1_brlt, clock_1_out, control_logic_1_asel, control_logic_1_brun,
       control_logic_1_bsel, control_logic_1_memrw, control_logic_1_regwen, PCSel, register_2_q;
  wire [1:0] control_logic_1_wbsel;
  wire [2:0] control_logic_1_immsel, funct3;
  wire [3:0] control_logic_1_alusel;
  wire [4:0] rd, rs1, rs2;
  wire [6:0] funct7, opcode;
  wire [31:0] adder_1_out, Arithmetic_Logic_Unit_result, DMEM_p5, imm_gen_1_imm, multiplexer_1_out,
       multiplexer_3_out, multiplexer_4_out, multiplexer_5_out, RegFile_read_data_1, RegFile_read_data_2,
       register_1_q, register_3_q;

  // Probe on PCSel
  control_logic control_logic_1 (
    .BSel(control_logic_1_bsel), .RegWEn(control_logic_1_regwen), .ASel(control_logic_1_asel),
    .ImmSel(control_logic_1_immsel), .BrUn(control_logic_1_brun), .PCSel(PCSel), .BrLt(branch_comp_1_brlt),
    .BrEq(branch_comp_1_breq), .inst({funct7, rs2, rs1, funct3, rd, opcode}),
    .ALUSel(control_logic_1_alusel), .MemRW(control_logic_1_memrw), .WBSel(control_logic_1_wbsel));
  Adder #(.width(32)) adder_1 (.a(PROGRAM_COUNTER), .b(32'h4), .out(adder_1_out));  // open: cin, cout
  // Probe on multiplexer_1_out
  Register #(.width(32)) register_1 (.D(INSTRUCTION), .clk(in_2), .Q(register_1_q));  // open: en, clr
  Register #(.width(1)) register_2 (.D(PCSel), .clk(in_2), .Q(register_2_q));  // open: en, clr
  Multiplexer #(.width(32), .enable("false")) multiplexer_1 (
    .in0(adder_1_out), .in1(Arithmetic_Logic_Unit_result), .out(multiplexer_1_out), .sel(PCSel));
  Register #(.width(32)) PC (.D(multiplexer_1_out), .clk(in_2), .Q(PROGRAM_COUNTER));  // open: en, clr
  Multiplexer #(.width(32), .enable("false")) multiplexer_2 (
    .in0(register_1_q), .in1(32'h13), .out({funct7, rs2, rs1, funct3, rd, opcode}), .sel(register_2_q));
  // Probe on {funct7, rs2, rs1, funct3, rd, opcode}
  imm_gen imm_gen_1 (
    .ImmSel(control_logic_1_immsel), .imm(imm_gen_1_imm), .inst({funct7, rs2, rs1, funct3, rd, opcode}));
  Register #(.width(32)) register_3 (.D(PROGRAM_COUNTER), .clk(in_2), .Q(register_3_q));  // open: en, clr
  // Probe on imm_gen_1_imm
  Clock clock_1 (.out(clock_1_out));
  regfile_main RegFile (
    .rs2(rs2), .rd(rd), .Read_Data_1(RegFile_read_data_1), .Read_Data_2(RegFile_read_data_2), .ra(ra),
    .sp(sp), .t0(t0), .t1(t1), .t2(t2), .s0(s0), .s1(s1), .a0(a0), .rs1(rs1), .Write_Data(multiplexer_5_out),
    .RegWEn(control_logic_1_regwen), .clk(in_2));
  branch_comp branch_comp_1 (
    .BrEq(branch_comp_1_breq), .BrUn(control_logic_1_brun), .rs1(RegFile_read_data_1),
    .BrLt(branch_comp_1_brlt), .rs2(RegFile_read_data_2));
  // Probe on RegFile_read_data_2
  Multiplexer #(.width(32), .enable("false")) multiplexer_3 (
    .in0(RegFile_read_data_1), .in1(register_3_q), .out(multiplexer_3_out), .sel(control_logic_1_asel));
  Multiplexer #(.width(32), .enable("false")) multiplexer_4 (
    .in0(RegFile_read_data_2), .in1(imm_gen_1_imm), .out(multiplexer_4_out), .sel(control_logic_1_bsel));
  // Probe on control_logic_1_bsel
  alu Arithmetic_Logic_Unit (
    .ALUSel(control_logic_1_alusel), .Result(Arithmetic_Logic_Unit_result), .A(multiplexer_3_out),
    .B(multiplexer_4_out));
  // Probe on Arithmetic_Logic_Unit_result
  // mem_main DMEM: pin names not known; wires that end beside it: Arithmetic_Logic_Unit_result, RegFile_read_data_2, in_2, control_logic_1_memrw, DMEM_p5
  // Probe on multiplexer_5_out
  Multiplexer #(.select(2), .width(32), .enable("false")) multiplexer_5 (
    .in0(Arithmetic_Logic_Unit_result), .in1(DMEM_p5), .in2(PROGRAM_COUNTER), .out(multiplexer_5_out),
    .sel(control_logic_1_wbsel));  // open: in3

  // Other names for the same wires on the sheet: clk = in_2

  // Notes on the sheet:
  //   Output
  //   IMEM (do **NOT** move this)
  //   Inputs
  //   Inputs/Outputs for testing. Do **NOT** move these.
endmodule
